# Fritzing sketch SinglePixelCameraWiring (saved by Fritzing 0.9.3b)

parts:
  Part1 = Arduino Uno (Rev3) - ICSP
  MOTOR3 = 28BYJ-48 Stepper Motor
  BREAKOUT2 = ULN2003A breakout board
  MOTOR4 = 28BYJ-48 Stepper Motor
  BREAKOUT3 = ULN2003A breakout board
  Part2 = Adafruit TCS34725 RGB Color Sensor [part_number="Adafruit #1334"]

nets:
  N1: Part1.A4/SDA, Part2.SDA
  N2: Part1.A5/SCL, Part2.SCL
  N3: Part1.D8, BREAKOUT3.In_1
  N4: Part1.D9_PWM, BREAKOUT3.In_2
  N5: Part1.D10_PWM/SS, BREAKOUT3.In_3
  N6: Part1.D11_PWM/MOSI, BREAKOUT3.In_4
  N7: Part1.D4, BREAKOUT2.In_1
  N8: Part1.D5_PWM, BREAKOUT2.In_2
  N9: Part1.D6_PWM, BREAKOUT2.In_3
  N10: Part1.D7, BREAKOUT2.In_4
  5V: Part1.5V, Part2.VIN
  N11: MOTOR3.RED, BREAKOUT2.BLUE_wire
  N12: MOTOR3.ORANGE, BREAKOUT2.PINK_wire
  N13: MOTOR3.YELLOW, BREAKOUT2.YELLOW_wire
  N14: MOTOR3.PINK, BREAKOUT2.ORANGE_wire
  N15: MOTOR3.BLUE, BREAKOUT2.RED_wire
  N16: MOTOR4.RED, BREAKOUT3.BLUE_wire
  N17: MOTOR4.ORANGE, BREAKOUT3.PINK_wire
  N18: MOTOR4.YELLOW, BREAKOUT3.YELLOW_wire
  N19: MOTOR4.PINK, BREAKOUT3.ORANGE_wire
  N20: MOTOR4.BLUE, BREAKOUT3.RED_wire
  N21: Part2.GND, Part2.LED_EN

custom parts:
  ULN2003A breakout board: ULN2003A 7-way Darlington Transistor Driver on breakoutboard
  Adafruit TCS34725 RGB Color Sensor: Your electronics can now see in dazzling color with this lovely color light sensor. We found the best color sensor on the market, the TCS34725, which has RGB and Clear light sensing elements. An IR blocking filter, integrated on-chip and localized to the color sensing photodiodes, minimizes the IR spectral component of the incoming light and allows color measurements to be made accurately. The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
